// Logisim project ProcessorNamık.circ as structural Verilog: 7 circuits, main circuit SR Latch
module SR_Latch (
  input  S__set,
  input  R__reset,
  output Q
);

  wire nor_1_out;

  nor nor_1 (nor_1_out, S__set, Q);
  nor nor_2 (Q, nor_1_out, R__reset);
endmodule

module D_Latch (
  input  D,
  input  clk,
  output Q
);

  wire and_1_out, and_2_out, not_1_out;

  not not_1 (not_1_out, D);
  and and_1 (and_1_out, D, clk);
  and and_2 (and_2_out, clk, not_1_out);
  SR_Latch SR_Latch (.S__set(and_1_out), .R__reset(and_2_out), .Q(Q));
endmodule

module D_Flip_Flop (
  input  D,
  input  clk,
  output Q
);

  wire D_Latch__master_q, not_1_out;

  not not_1 (not_1_out, clk);
  D_Latch D_Latch__master (.D(D), .clk(not_1_out), .Q(D_Latch__master_q));
  D_Latch D_Latch__servant (.D(D_Latch__master_q), .clk(clk), .Q(Q));
endmodule

// 2 R
module _2_bit_Register (
  input  I1,
  input  I0,
  input  clk,
  output Q1,
  output Q0
);

  D_Flip_Flop Flip_Flop (.D(I1), .clk(clk), .Q(Q1));
  D_Flip_Flop Flip_Flop_2 (.D(I0), .clk(clk), .Q(Q0));
endmodule

module _4_bit_Register (
  input  I3,
  input  I2,
  input  I1,
  input  I0,
  input  clk,
  output Q3,
  output Q2,
  output Q1,
  output Q0
);

  _2_bit_Register u_2_bit_register_1 (.clk(clk), .I1(I3), .I0(I2), .Q1(Q3), .Q0(Q2));
  _2_bit_Register u_2_bit_register_2 (.clk(clk), .I1(I1), .I0(I0), .Q1(Q1), .Q0(Q0));
endmodule

module _8_bit_Register (
  input  I7,
  input  I6,
  input  I5,
  input  I4,
  input  I3,
  input  I2,
  input  I1,
  input  I0,
  input  clk,
  output Q7,
  output Q6,
  output Q5,
  output Q4,
  output Q3,
  output Q2,
  output Q1,
  output Q0
);

  _4_bit_Register u_4_bit_register_1 (
    .clk(clk), .I3(I7), .I2(I6), .I1(I5), .I0(I4), .Q3(Q7), .Q2(Q6), .Q1(Q5), .Q0(Q4));
  _4_bit_Register u_4_bit_register_2 (
    .clk(clk), .I3(I3), .I2(I2), .I1(I1), .I0(I0), .Q3(Q3), .Q2(Q2), .Q1(Q1), .Q0(Q0));
endmodule

module _12_bit_register (
  input  I11,
  input  I10,
  input  I9,
  input  I8,
  input  I7,
  input  I6,
  input  I5,
  input  I4,
  input  I3,
  input  I2,
  input  I1,
  input  I0,
  input  clk,
  output Q11,
  output Q10,
  output Q9,
  output Q8,
  output Q7,
  output Q6,
  output Q5,
  output Q4,
  output Q3,
  output Q2,
  output Q1,
  output Q0
);

  _8_bit_Register u_8_bit_register_1 (
    .clk(clk), .I7(I11), .I6(I10), .I5(I9), .I4(I8), .I3(I7), .I2(I6), .I1(I5), .I0(I4), .Q7(Q11), .Q6(Q10),
    .Q5(Q9), .Q4(Q8), .Q3(Q7), .Q2(Q6), .Q1(Q5), .Q0(Q4));
  _4_bit_Register u_4_bit_register_1 (
    .clk(clk), .I3(I3), .I2(I2), .I1(I1), .I0(I0), .Q3(Q3), .Q2(Q2), .Q1(Q1), .Q0(Q0));
endmodule
